# Fritzing sketch CyGarage (saved by Fritzing 0.9.3b)
circuit board: 9.21719cm x 6.15156cm
breadboards: 1

parts:
  LED2 = LED - 5mm [color="Red (633nm)" package="5 mm [THT]"]
  LED1 = LED - 5mm [color="Green (555nm)" package="5 mm [THT]"]
  J1 = Screw terminal - 2 pins [package=THT]
  J3 = Screw terminal - 2 pins [package=THT]
  J2 = Screw terminal - 2 pins [package=THT]
  R1 = Resistor [tolerance=±5% resistance=330 package=THT]
  R2 = Resistor [tolerance=±5% resistance=330 package=THT]
  DC1 = Reed switch [package=THT]  # not connected
  DC2 = Reed switch [package=THT]  # not connected
  Part1 = Adafruit PowerRelay Feather Wing [part_number="Adafruit #3191"]
  Adafruit_HUZZAH_ESP8266_Breakout = Adafruit HUZZAH ESP8266 Breakout [part_number=2471]

nets:
  GND: LED2.cathode, LED1.cathode, J1.pin1, J3.pin1, J2.pin2, Part1.GND, Adafruit_HUZZAH_ESP8266_Breakout.GND
  N1: LED2.anode, Adafruit_HUZZAH_ESP8266_Breakout.#5
  N2: LED1.anode, Adafruit_HUZZAH_ESP8266_Breakout.#2
  N3: J1.pin2, R1.Pin_1, R2.Pin_1, Adafruit_HUZZAH_ESP8266_Breakout.V+
  N4: J3.pin2, R2.Pin_0, Adafruit_HUZZAH_ESP8266_Breakout.#13
  N5: J2.pin1, R1.Pin_0, Adafruit_HUZZAH_ESP8266_Breakout.#12
  N6: Part1.3.3V, Adafruit_HUZZAH_ESP8266_Breakout.3V
  N7: Part1.A, Adafruit_HUZZAH_ESP8266_Breakout.#4

notes:
  CyGarage, CyGarage Main Board. IoT garage door integration., 1.0
  CyGarage Rev 1.0
  5VDC 1A
  DC1
  -  +
  DC2
  WiFi Act
  Open/Ajar
  DC1 and DC2 are external components and should not be printed on the PCB.

custom parts:
  Adafruit PowerRelay Feather Wing: A Feather board without ambition is a Feather board without FeatherWings! This is the Power Relay FeatherWing. It gives you power to control, and control over power. Put simply, you can now turn on and off lamps, fans, solenoids, and other small appliances that run on up to 250VAC or DC power using any Feather board. Compared to our smaller Relay FeatherWings, this one can handle a beefy 1200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
